// Logisim project ALU16-Hack.circ as structural Verilog
module ALU (
  input  NX,
  input  NX_2,
  input  ZY,
  input  NY,
  input  F,
  input  NO,
  input  [15:0] X,
  input  [15:0] Y,
  output [15:0] Out,
  output NG,
  output ZR
);

  wire or_1_out;
  wire [15:0] adder_1_out, and_1_out, multiplexer_1_out, multiplexer_2_out, multiplexer_3_out,
       multiplexer_4_out, multiplexer_5_out, not_1_out, not_2_out, not_4_out;

  Multiplexer #(.width(16), .enable("false")) multiplexer_1 (
    .in0(X), .in1({16{1'b0}}), .out(multiplexer_1_out), .sel(NX));
  Multiplexer #(.width(16), .enable("false")) multiplexer_2 (
    .in0(Y), .in1({16{1'b0}}), .out(multiplexer_2_out), .sel(ZY));
  Multiplexer #(.width(16), .enable("false")) multiplexer_3 (
    .in0(multiplexer_1_out), .in1(not_1_out), .out(multiplexer_3_out), .sel(NX_2));
  assign not_1_out = ~multiplexer_1_out;  // NOT_Gate not_1, 16 bits wide
  Multiplexer #(.width(16), .enable("false")) multiplexer_4 (
    .in0(multiplexer_2_out), .in1(not_2_out), .out(multiplexer_4_out), .sel(NY));
  assign not_2_out = ~multiplexer_2_out;  // NOT_Gate not_2, 16 bits wide
  assign and_1_out = multiplexer_3_out & multiplexer_4_out;  // AND_Gate and_1, 16 bits wide
  Adder #(.width(16)) adder_1 (.a(multiplexer_3_out), .b(multiplexer_4_out), .out(adder_1_out));  // open: cin, cout
  or or_1 (or_1_out, NG, Out[14], Out[13], Out[12], Out[11], Out[10], Out[9], Out[8], Out[7], Out[6], Out[5], Out[4], Out[3], Out[2], Out[1], Out[0]);
  not not_3 (ZR, or_1_out);
  Multiplexer #(.width(16), .enable("false")) multiplexer_5 (
    .in0(and_1_out), .in1(adder_1_out), .out(multiplexer_5_out), .sel(F));
  Multiplexer #(.width(16), .enable("false")) multiplexer_6 (
    .in0(multiplexer_5_out), .in1(not_4_out), .out({NG, Out[14:0]}), .sel(NO));
  assign not_4_out = ~multiplexer_5_out;  // NOT_Gate not_4, 16 bits wide

  assign Out[15] = NG;
endmodule

module ALU_Test (
  input  in_1,
  input  in_2,
  input  in_3,
  input  in_4,
  input  in_5,
  input  in_6,
  input  [15:0] in_7,
  input  [15:0] in_8,
  output [15:0] out_9,
  output out_10,
  output out_11
);

  ALU alu_1 (
    .X(in_7), .Y(in_8), .Out(out_9), .NX_2(in_2), .ZY(in_3), .NY(in_4), .F(in_5), .NO(in_6), .NG(out_10),
    .ZR(out_11), .NX(in_1));
endmodule

module CPU (
  input  Clock,
  input  [15:0] Intruct,
  input  [15:0] InM,
  input  in_4,
  output [15:0] OutM,
  output writeM,
  output [14:0] addressM,
  output [14:0] PC
);

  wire and_7_out, and_9_out, and_10_out, demultiplexer_1_out0, demultiplexer_1_out1, demultiplexer_1_out2,
       demultiplexer_1_out3, demultiplexer_1_out4, demultiplexer_1_out5, demultiplexer_1_out6, NG, not_1_out,
       not_2_out, not_3_out, not_4_out, not_5_out, not_6_out, not_7_out, not_8_out, or_1_out, or_2_out,
       or_3_out, ZR;
  wire [6:0] Jump;
  wire [15:0] D_q, multiplexer_1_out, multiplexer_2_out;
  wire [15:15] A_q, PC_q;

  not not_1 (not_1_out, Intruct[15]);
  Multiplexer #(.width(16), .enable("false")) multiplexer_1 (
    .in0(OutM), .in1(Intruct), .out(multiplexer_1_out), .sel(not_1_out));
  not not_2 (not_2_out, or_3_out);
  Demultiplexer #(.select(3), .enable("false")) demultiplexer_1 (
    .out0(demultiplexer_1_out0), .out1(demultiplexer_1_out1), .out2(demultiplexer_1_out2),
    .out3(demultiplexer_1_out3), .out4(demultiplexer_1_out4), .out5(demultiplexer_1_out5),
    .out6(demultiplexer_1_out6), .out7(Jump[0]), .in(1'b1), .sel(Intruct[2:0]));
  Register #(.width(16)) D (.D(OutM), .en(and_9_out), .Q(D_q), .clk(Clock));  // open: clr
  Register #(.width(16)) A (.D(multiplexer_1_out), .en(or_2_out), .Q({A_q[15], addressM}), .clk(Clock));  // open: clr
  Counter #(.width(16), .max('hffff)) u_PC (
    .load(or_3_out), .D({A_q[15], addressM}), .count(not_2_out), .Q({PC_q[15], PC}), .clk(Clock), .clr(in_4));  // open: carry
  Multiplexer #(.width(16), .enable("false")) multiplexer_2 (
    .in0({A_q[15], addressM}), .in1(InM), .out(multiplexer_2_out), .sel(and_10_out));
  not not_3 (not_3_out, NG);
  and and_1 (Jump[1], demultiplexer_1_out1, not_3_out, not_4_out);
  not not_4 (not_4_out, ZR);
  and and_2 (Jump[2], demultiplexer_1_out2, not_5_out, ZR);
  not not_5 (not_5_out, NG);
  not not_6 (not_6_out, NG);
  and and_3 (Jump[3], demultiplexer_1_out3, not_6_out);
  and and_4 (Jump[4], demultiplexer_1_out4, NG, not_7_out);
  not not_7 (not_7_out, ZR);
  not not_8 (not_8_out, ZR);
  and and_5 (Jump[5], demultiplexer_1_out5, not_8_out);
  and and_6 (Jump[6], demultiplexer_1_out6, or_1_out);
  or or_1 (or_1_out, NG, ZR);
  and and_7 (and_7_out, Intruct[5], Intruct[15]);
  ALU alu_1 (
    .X(D_q), .Y(multiplexer_2_out), .Out(OutM), .NX_2(Intruct[10]), .ZY(Intruct[9]), .NY(Intruct[8]),
    .F(Intruct[7]), .NO(Intruct[6]), .NG(NG), .ZR(ZR), .NX(Intruct[11]));
  and and_8 (writeM, Intruct[3], Intruct[15]);
  and and_9 (and_9_out, Intruct[4], Intruct[15]);
  or or_2 (or_2_out, and_7_out, not_1_out);
  and and_10 (and_10_out, Intruct[12], Intruct[15]);
  or or_3 (or_3_out, Jump[0], Jump[1], Jump[2], Jump[3], Jump[4], Jump[5], Jump[6]);
endmodule
