// Logisim project LittleDrop.circ as structural Verilog: 18 circuits, main circuit main
module main (
  input  [7:0] in_1,
  input  in_2,
  input  in_3,
  output [7:0] out_4,
  output [7:0] out_5
);

  wire clock_1_out;
  wire [7:0] demultiplexer_1_out0, demultiplexer_1_out1;

  Clock clock_1 (.out(clock_1_out));
  Demultiplexer #(.width(8)) demultiplexer_1 (
    .out0(demultiplexer_1_out0), .out1(demultiplexer_1_out1), .in(in_1), .sel(in_3), .en(in_2));
  _8_bit_Register u_8_bit_register_1 (.in_1(demultiplexer_1_out0), .Clock(clock_1_out), .Load(in_2), .out_4(out_4));
  _8_bit_Register u_8_bit_register_2 (.in_1(demultiplexer_1_out1), .Clock(clock_1_out), .Load(in_2), .out_4(out_5));
endmodule

module HA (
  input  a,
  input  b,
  output S,
  output Cout
);

  xor xor_1 (S, a, b);
  and and_1 (Cout, a, b);
endmodule

module FA (
  input  a,
  input  b,
  input  Cin,
  output S,
  output Cout
);

  wire and_1_out, and_2_out, xor_1_out;

  xor xor_1 (xor_1_out, a, b);
  and and_1 (and_1_out, xor_1_out, Cin);
  and and_2 (and_2_out, a, b);
  xor xor_2 (S, xor_1_out, Cin);
  or or_1 (Cout, and_1_out, and_2_out);
endmodule

module NOR_FF (
  input  Reset,
  input  Set,
  output Q,
  output Q_prime
);

  nor nor_1 (Q, Reset, Q_prime);
  nor nor_2 (Q_prime, Q, Set);
endmodule

module NAND_FF (
  input  Reset,
  input  Set,
  output Q,
  output Q_prime
);

  nand nand_1 (Q, Reset, Q_prime);
  nand nand_2 (Q_prime, Q, Set);
endmodule

module D_FF (
  input  D,
  input  Clock,
  output Q,
  output Q_prime
);

  wire nand_1_out, nand_2_out, not_1_out;

  not not_1 (not_1_out, D);
  nand nand_1 (nand_1_out, D, Clock);
  nand nand_2 (nand_2_out, Clock, not_1_out);
  nand nand_3 (Q, nand_1_out, Q_prime);
  nand nand_4 (Q_prime, nand_2_out, Q);
endmodule

module J_K_FF (
  input  J,
  input  Clock,
  input  K,
  output Q,
  output Q_prime
);

  wire and_1_out, and_2_out;

  and and_1 (and_1_out, Q, J, Clock);
  and and_2 (and_2_out, Clock, K, Q_prime);
  nor nor_1 (Q, and_1_out, Q_prime);
  nor nor_2 (Q_prime, Q, and_2_out);
endmodule

module T_FF (
  input  T,
  input  Clock,
  output Q,
  output Q_prime
);

  wire and_1_out, and_2_out;

  and and_1 (and_1_out, Q, T, Clock);
  and and_2 (and_2_out, Clock, T, Q_prime);
  nor nor_1 (Q, and_1_out, Q_prime);
  nor nor_2 (Q_prime, Q, and_2_out);
endmodule

module Transition (
  input  Clock,
  output Clock_prime
);

  wire not_1_out;

  not not_1 (not_1_out, Clock);
  and and_1 (Clock_prime, not_1_out, Clock);
endmodule

// 8-bit Register
module _8_bit_Register_test (
  input  D7,
  input  D6,
  input  D5,
  input  D4,
  input  D3,
  input  D2,
  input  D1,
  input  D0,
  input  Clock,
  input  Load,
  output out_11,
  output out_12,
  output out_13,
  output out_14,
  output out_15,
  output out_16,
  output out_17,
  output out_18
);

  Bit bit_1 (.In(D7), .Load(Load), .Out(out_11), .Clock(Clock));
  Bit bit_2 (.In(D6), .Load(Load), .Out(out_12), .Clock(Clock));
  Bit bit_3 (.In(D5), .Load(Load), .Out(out_13), .Clock(Clock));
  Bit bit_4 (.In(D4), .Load(Load), .Out(out_14), .Clock(Clock));
  Bit bit_5 (.In(D3), .Load(Load), .Out(out_15), .Clock(Clock));
  Bit bit_6 (.In(D1), .Load(Load), .Out(out_17), .Clock(Clock));
  Bit bit_7 (.In(D2), .Load(Load), .Out(out_16), .Clock(Clock));
  Bit bit_8 (.In(D0), .Load(Load), .Out(out_18), .Clock(Clock));
endmodule

module _8_bit_Register (
  input  [7:0] in_1,
  input  Clock,
  input  Load,
  output [7:0] out_4
);

  Bit bit_1 (.In(in_1[7]), .Load(Load), .Out(out_4[7]), .Clock(Clock));
  Bit bit_2 (.In(in_1[6]), .Load(Load), .Out(out_4[6]), .Clock(Clock));
  Bit bit_3 (.In(in_1[5]), .Load(Load), .Out(out_4[5]), .Clock(Clock));
  Bit bit_4 (.In(in_1[4]), .Load(Load), .Out(out_4[4]), .Clock(Clock));
  Bit bit_5 (.In(in_1[3]), .Load(Load), .Out(out_4[3]), .Clock(Clock));
  Bit bit_6 (.In(in_1[2]), .Load(Load), .Out(out_4[2]), .Clock(Clock));
  Bit bit_7 (.In(in_1[1]), .Load(Load), .Out(out_4[1]), .Clock(Clock));
  Bit bit_8 (.In(in_1[0]), .Load(Load), .Out(out_4[0]), .Clock(Clock));
endmodule

module Mux2Way (
  input  A,
  input  B,
  input  Sel,
  output Out
);

  wire and_with_nand_1_out_3, and_with_nand_2_out_3, not_with_nand_1_out_2;

  NOT_with_NAND not_with_nand_1 (.in_1(Sel), .out_2(not_with_nand_1_out_2));
  AND_with_NAND and_with_nand_1 (.in_1(A), .in_2(not_with_nand_1_out_2), .out_3(and_with_nand_1_out_3));
  AND_with_NAND and_with_nand_2 (.in_1(B), .in_2(Sel), .out_3(and_with_nand_2_out_3));
  OR_with_NAND or_with_nand_1 (.in_1(and_with_nand_1_out_3), .in_2(and_with_nand_2_out_3), .out_3(Out));
endmodule

module NOT_with_NAND (
  input  in_1,
  output out_2
);

  nand nand_1 (out_2, in_1, in_1);
endmodule

module AND_with_NAND (
  input  in_1,
  input  in_2,
  output out_3
);

  wire nand_1_out;

  nand nand_1 (nand_1_out, in_1, in_2);
  nand nand_2 (out_3, nand_1_out, nand_1_out);
endmodule

module OR_with_NAND (
  input  in_1,
  input  in_2,
  output out_3
);

  wire nand_1_out, nand_2_out;

  nand nand_1 (nand_1_out, in_1, in_1);
  nand nand_2 (nand_2_out, in_2, in_2);
  nand nand_3 (out_3, nand_1_out, nand_2_out);
endmodule

module XOR_with_NAND (
  input  in_1,
  input  in_2,
  output out_3
);

  wire nand_1_out, nand_2_out, nand_3_out, nand_4_out;

  nand nand_1 (nand_1_out, in_1, in_1);
  nand nand_2 (nand_2_out, in_2, in_2);
  nand nand_3 (nand_3_out, in_1, nand_2_out);
  nand nand_4 (nand_4_out, nand_1_out, in_2);
  nand nand_5 (out_3, nand_3_out, nand_4_out);
endmodule

module Dmux2Way (
  input  IN,
  input  SEL,
  output A,
  output B
);

  wire not_with_nand_1_out_2;

  NOT_with_NAND not_with_nand_1 (.in_1(SEL), .out_2(not_with_nand_1_out_2));
  AND_with_NAND and_with_nand_1 (.in_1(IN), .in_2(not_with_nand_1_out_2), .out_3(A));
  AND_with_NAND and_with_nand_2 (.in_1(IN), .in_2(SEL), .out_3(B));
endmodule

module Bit (
  input  In,
  input  Load,
  input  Clock,
  output Out
);

  wire mux2way_1_out;

  Mux2Way mux2way_1 (.A(Out), .B(In), .Out(mux2way_1_out), .Sel(Load));
  D_FF d_ff_1 (.D(mux2way_1_out), .Clock(Clock), .Q(Out));  // open: Q_prime
endmodule
